// Logisim project 1-bit 2x1 MUX.circ as structural Verilog: 5 circuits, main circuit main
module main (
  input  in_1,
  input  in_2,
  input  in_3,
  output out_4
);

  wire and_1_out, and_2_out, not_1_out;

  not not_1 (not_1_out, in_3);
  and and_1 (and_1_out, in_1, not_1_out);
  or or_1 (out_4, and_1_out, and_2_out);
  and and_2 (and_2_out, in_2, in_3);
endmodule

module _2_bit_2x1_MUX (
  input  in_1,
  input  in_2,
  input  in_3,
  input  in_4,
  input  in_5,
  input  in_6,
  input  in_7,
  output out_8,
  output out_9,
  output out_10
);

  main main_1 (.in_1(in_1), .in_2(in_2), .in_3(in_7), .out_4(out_8));
  main main_2 (.in_1(in_3), .in_2(in_4), .in_3(in_7), .out_4(out_9));
  main main_3 (.in_1(in_5), .in_2(in_6), .in_3(in_7), .out_4(out_10));
endmodule

module half_adder (
  input  in_1,
  input  in_2,
  output out_3,
  output out_4
);

  xor xor_1 (out_3, in_1, in_2);
  and and_1 (out_4, in_1, in_2);
endmodule

module full_adder (
  input  in_1,
  input  in_2,
  input  in_3,
  output out_4,
  output out_5
);

  wire half_adder_1_out_3, half_adder_1_out_4, half_adder_2_out_4;

  half_adder half_adder_1 (.in_1(in_1), .in_2(in_2), .out_3(half_adder_1_out_3), .out_4(half_adder_1_out_4));
  half_adder half_adder_2 (.in_1(half_adder_1_out_3), .in_2(in_3), .out_3(out_4), .out_4(half_adder_2_out_4));
  or or_1 (out_5, half_adder_2_out_4, half_adder_1_out_4);
endmodule

module _32_bit_binary_ripple_carry (
  input  in_1,
  input  in_2,
  output out_3
);

  wire full_adder_2_out_5, full_adder_3_out_5, full_adder_4_out_5, full_adder_5_out_5, full_adder_6_out_5,
       full_adder_7_out_5, full_adder_8_out_5, full_adder_9_out_5, full_adder_10_out_5, full_adder_11_out_5,
       full_adder_12_out_5, full_adder_13_out_5, full_adder_14_out_5, full_adder_15_out_5,
       full_adder_16_out_5, full_adder_17_out_5, full_adder_18_out_5, full_adder_19_out_5,
       full_adder_20_out_5, full_adder_21_out_5, full_adder_22_out_5, full_adder_23_out_5,
       full_adder_24_out_5, full_adder_25_out_5, full_adder_26_out_5, full_adder_27_out_5,
       full_adder_28_out_5, full_adder_29_out_5, full_adder_30_out_5, full_adder_31_out_5,
       full_adder_32_out_5, undriven;

  xor xor_1 (out_3, in_1, in_2);
  full_adder full_adder_1 (.in_3(full_adder_2_out_5));  // open: in_1, in_2, out_4, out_5
  full_adder full_adder_2 (.in_3(full_adder_3_out_5), .out_5(full_adder_2_out_5));  // open: in_1, in_2, out_4
  full_adder full_adder_3 (.in_3(full_adder_4_out_5), .out_5(full_adder_3_out_5));  // open: in_1, in_2, out_4
  full_adder full_adder_4 (.in_3(full_adder_5_out_5), .out_5(full_adder_4_out_5));  // open: in_1, in_2, out_4
  full_adder full_adder_5 (.in_3(full_adder_6_out_5), .out_5(full_adder_5_out_5));  // open: in_1, in_2, out_4
  full_adder full_adder_6 (.in_3(full_adder_7_out_5), .out_5(full_adder_6_out_5));  // open: in_1, in_2, out_4
  full_adder full_adder_7 (.in_3(full_adder_8_out_5), .out_5(full_adder_7_out_5));  // open: in_1, in_2, out_4
  full_adder full_adder_8 (.in_3(full_adder_9_out_5), .out_5(full_adder_8_out_5));  // open: in_1, in_2, out_4
  full_adder full_adder_9 (.in_3(full_adder_10_out_5), .out_5(full_adder_9_out_5));  // open: in_1, in_2, out_4
  full_adder full_adder_10 (.in_3(full_adder_11_out_5), .out_5(full_adder_10_out_5));  // open: in_1, in_2, out_4
  full_adder full_adder_11 (.in_3(full_adder_12_out_5), .out_5(full_adder_11_out_5));  // open: in_1, in_2, out_4
  full_adder full_adder_12 (.in_3(full_adder_13_out_5), .out_5(full_adder_12_out_5));  // open: in_1, in_2, out_4
  full_adder full_adder_13 (.in_3(full_adder_14_out_5), .out_5(full_adder_13_out_5));  // open: in_1, in_2, out_4
  full_adder full_adder_14 (.in_3(full_adder_15_out_5), .out_5(full_adder_14_out_5));  // open: in_1, in_2, out_4
  full_adder full_adder_15 (.in_3(full_adder_16_out_5), .out_5(full_adder_15_out_5));  // open: in_1, in_2, out_4
  full_adder full_adder_16 (.in_3(full_adder_17_out_5), .out_5(full_adder_16_out_5));  // open: in_1, in_2, out_4
  full_adder full_adder_17 (.in_3(full_adder_18_out_5), .out_5(full_adder_17_out_5));  // open: in_1, in_2, out_4
  full_adder full_adder_18 (.in_3(full_adder_19_out_5), .out_5(full_adder_18_out_5));  // open: in_1, in_2, out_4
  full_adder full_adder_19 (.in_3(full_adder_20_out_5), .out_5(full_adder_19_out_5));  // open: in_1, in_2, out_4
  full_adder full_adder_20 (.in_3(full_adder_21_out_5), .out_5(full_adder_20_out_5));  // open: in_1, in_2, out_4
  full_adder full_adder_21 (.in_3(full_adder_22_out_5), .out_5(full_adder_21_out_5));  // open: in_1, in_2, out_4
  full_adder full_adder_22 (.in_3(full_adder_23_out_5), .out_5(full_adder_22_out_5));  // open: in_1, in_2, out_4
  full_adder full_adder_23 (.in_3(full_adder_24_out_5), .out_5(full_adder_23_out_5));  // open: in_1, in_2, out_4
  full_adder full_adder_24 (.in_3(full_adder_25_out_5), .out_5(full_adder_24_out_5));  // open: in_1, in_2, out_4
  full_adder full_adder_25 (.in_3(full_adder_26_out_5), .out_5(full_adder_25_out_5));  // open: in_1, in_2, out_4
  full_adder full_adder_26 (.in_3(full_adder_27_out_5), .out_5(full_adder_26_out_5));  // open: in_1, in_2, out_4
  full_adder full_adder_27 (.in_3(full_adder_28_out_5), .out_5(full_adder_27_out_5));  // open: in_1, in_2, out_4
  full_adder full_adder_28 (.in_3(full_adder_29_out_5), .out_5(full_adder_28_out_5));  // open: in_1, in_2, out_4
  full_adder full_adder_29 (.in_3(full_adder_30_out_5), .out_5(full_adder_29_out_5));  // open: in_1, in_2, out_4
  full_adder full_adder_30 (.in_3(full_adder_31_out_5), .out_5(full_adder_30_out_5));  // open: in_1, in_2, out_4
  full_adder full_adder_31 (.in_3(full_adder_32_out_5), .out_5(full_adder_31_out_5));  // open: in_1, in_2, out_4
  full_adder full_adder_32 (.in_3(undriven), .out_5(full_adder_32_out_5));  // open: in_1, in_2, out_4
endmodule
