// Logisim project ShifterModel.circ as structural Verilog: 2 circuits, main circuit main
module main (
  input  D2,
  input  SI,
  input  [1:0] M,
  input  D1,
  input  D0,
  output SO_L,
  output Q3,
  output Q1,
  output Q0,
  output SO_R
);

  wire clock_1_out, n4x1_1_out_6, n4x1_2_out_6, n4x1_3_out_6, register_1_q;

  Clock clock_1 (.out(clock_1_out));
  _4x1 u_4x1_1 (.out_6(n4x1_1_out_6), .in_5(M), .in_1(Q3), .in_2(SI), .in_3(D2), .in_4(Q3));
  _4x1 u_4x1_2 (.out_6(n4x1_2_out_6), .in_5(M), .in_1(Q1), .in_2(Q3), .in_3(D1), .in_4(Q1));
  _4x1 u_4x1_3 (.out_6(n4x1_3_out_6), .in_5(M), .in_1(Q0), .in_2(Q1), .in_3(D0), .in_4(Q0));
  Register #(.width(1)) register_1 (.Q(register_1_q));  // open: D, en, clk, clr
  _1_reg u_1_reg_1 (
    .Preset(register_1_q), .Data(n4x1_1_out_6), .Load(register_1_q), .Reset(register_1_q),
    .Clock(clock_1_out), .out_6(Q3));
  _1_reg u_1_reg_2 (
    .Preset(register_1_q), .Data(n4x1_2_out_6), .Load(register_1_q), .Reset(register_1_q),
    .Clock(clock_1_out), .out_6(Q1));
  _1_reg u_1_reg_3 (
    .Preset(register_1_q), .Data(n4x1_3_out_6), .Load(register_1_q), .Reset(register_1_q),
    .Clock(clock_1_out), .out_6(Q0));

  assign SO_L = Q3;
  assign SO_R = Q0;

  // Notes on the sheet:
  //   CLK
endmodule

module _4x1 (
  input  in_1,
  input  in_2,
  input  in_3,
  input  in_4,
  input  [1:0] in_5,
  output out_6
);

  wire multiplexer_1_out, multiplexer_2_out;

  Multiplexer #(.enable("false")) multiplexer_1 (.in0(in_1), .in1(in_2), .out(multiplexer_1_out), .sel(in_5[0]));
  Multiplexer #(.enable("false")) multiplexer_2 (.in0(in_3), .in1(in_4), .out(multiplexer_2_out), .sel(in_5[0]));
  Multiplexer #(.enable("false")) multiplexer_3 (
    .in0(multiplexer_1_out), .in1(multiplexer_2_out), .out(out_6), .sel(in_5[1]));
endmodule
