// Logisim project 1-bit flip flop.circ as structural Verilog: 5 circuits, main circuit main
module main (
  input  Prst,
  input  Data,
  input  Clock,
  input  Reset,
  output Q,
  output Q_prime
);

  wire nand_1_out, nand_2_out, nand_3_out, nand_4_out, nand_5_out, nand_6_out;

  nand nand_1 (nand_1_out, Data, Clock);
  nand nand_2 (nand_2_out, Clock, ~Data);  // NAND_Gate
  nand nand_3 (nand_3_out, Prst, nand_1_out, nand_4_out);
  nand nand_4 (nand_4_out, nand_3_out, nand_2_out, Reset);
  nand nand_5 (nand_5_out, nand_3_out, ~Clock);  // NAND_Gate
  nand nand_6 (nand_6_out, ~Clock, nand_4_out);  // NAND_Gate
  nand nand_7 (Q, Prst, nand_5_out, Q_prime);
  nand nand_8 (Q_prime, Q, nand_6_out, Reset);

  // Notes on the sheet:
  //   1-bit flip flop
endmodule

module _1_reg (
  input  Preset,
  input  Data,
  input  Load,
  input  Reset,
  input  Clock,
  output out_6
);

  wire multiplexer_1_out;

  Multiplexer #(.enable("false")) multiplexer_1 (.in0(out_6), .in1(Data), .out(multiplexer_1_out), .sel(Load));
  main main_1 (.Prst(Preset), .Data(multiplexer_1_out), .Clock(Clock), .Reset(Reset), .Q(out_6));  // open: Q_prime
endmodule

module _32_Reg (
  input  in_1
);

  // _1_reg 1_reg_1: pin names not known; wires that end beside it: in_1, in_1
  // _1_reg 1_reg_2: pin names not known; wires that end beside it: in_1, in_1
  // _1_reg 1_reg_3: pin names not known; wires that end beside it: in_1, in_1
  // _1_reg 1_reg_4: pin names not known; wires that end beside it: in_1, in_1
  // _1_reg 1_reg_5: pin names not known; wires that end beside it: in_1, in_1
  // _1_reg 1_reg_6: pin names not known; wires that end beside it: in_1, in_1
  // _1_reg 1_reg_7: pin names not known; wires that end beside it: in_1, in_1
  // _1_reg 1_reg_8: pin names not known; wires that end beside it: in_1, in_1
  // _1_reg 1_reg_9: pin names not known; wires that end beside it: in_1, in_1
  // _1_reg 1_reg_10: pin names not known; wires that end beside it: in_1, in_1
  // _1_reg 1_reg_11: pin names not known; wires that end beside it: in_1, in_1
  // _1_reg 1_reg_12: pin names not known; wires that end beside it: in_1, in_1
  // _1_reg 1_reg_13: pin names not known; wires that end beside it: in_1, in_1
  // _1_reg 1_reg_14: pin names not known; wires that end beside it: in_1, in_1
  // _1_reg 1_reg_15: pin names not known; wires that end beside it: in_1, in_1
  _1_reg u_1_reg_16 ();  // open: Preset, Data, Load, Reset, Clock, out_6
endmodule

module Decoder (
);

  Decoder_part decoder_1 ();  // open: out0, out1, sel, en
endmodule

module Shifter (
);

  _1_reg u_1_reg_1 ();  // open: Preset, Data, Load, Reset, Clock, out_6
endmodule
